# Fritzing sketch Board (saved by Fritzing 0.9.9b)
breadboards: 1

parts:
  Part1 = Arduino Nano (Rev3.0)
  U1 = Voltage Regulator - 5V [package="TO220 [THT]"]
  VCC1 = Battery
  Q1 = PNP-Transistor [package="TO92 [THT]"]
  MIC1 = Microphone
  S1 = Pushbutton [package="[THT]"]
  Mod1 = Passive Buzzer
  HC-SR04_Sensor_1 = HC-SR04 Ultrasonic Distance Sensor
  Part3 = Bluetooth HC-05 Macho  # not connected
  Part4 = LSM303C (6 DOF)  # not connected
  R1 = Resistor [tolerance=±5% resistance=220 package="1206 [SMD]"]

nets:
  GND: Part1.GND, U1.GND, VCC1.-, MIC1.pin1, Mod1.-, HC-SR04_Sensor_1.GND, R1.Pin_0
  N1: Part1.D2, S1.Pin_1, S1.Pin_2, R1.Pin_1
  N2: Part1.D3, Mod1.S
  N3: Part1.D4, HC-SR04_Sensor_1.ECHO
  N4: Part1.D5, HC-SR04_Sensor_1.TRIG
  N5: Part1.D6, Q1.B
  N6: Part1.VIN, U1.output_voltage
  5V: Part1.5V, S1.Pin_3, S1.Pin_4, HC-SR04_Sensor_1.VCC
  N7: Part1.3V3, Q1.C
  N8: Q1.E, MIC1.pin2
